// Logisim project sequencer.circ as structural Verilog: 1 circuit, main circuit main
module main (
  input  CLK,
  input  [7:0] MAP
);

  wire [7:0] main_1_output, main_2_out, main_3_out, multiplexer_1_out;
  wire [17:0] rom_1_data;

  ADDER___8_BIT_main main_1 (.Input_1(main_3_out), .Input_2({8{1'b1}}), .Output(main_1_output));
  _8bit_D_Latch_main main_2 (.IN(main_1_output), .CLK(CLK), .OUT(main_2_out));  // open: CLR, EN
  Multiplexer #(.select(2), .width(8)) multiplexer_1 (
    .in0(MAP), .in1(main_1_output), .in2(main_2_out), .in3(rom_1_data[7:0]), .out(multiplexer_1_out));  // open: sel, en
  _8bit_D_Latch_main main_3 (.IN(multiplexer_1_out), .CLK(CLK), .OUT(main_3_out));  // open: CLR, EN
  ROM #(.dataWidth(18)) rom_1 (.addr(main_3_out), .data(rom_1_data));  // open: sel
endmodule
